# Fritzing sketch arduino-clock (saved by Fritzing 0.9.0b)
breadboards: 1

parts:
  Part1 = Arduino Uno (Rev3) - ICSP
  U1 = LCD-16X2 [package=lcd-16x2]
  ENC28J1 = ENC28J60
  R1 = Resistor [tolerance=±5% resistance=680 package=THT]

nets:
  GND: Part1.GND, U1.VSS, U1.R_W, U1.K, ENC28J1.GND, R1.Pin_1
  N1: Part1.D8, ENC28J1.CS
  N2: Part1.D11_PWM/MOSI, ENC28J1.SI
  N3: Part1.D12/MISO, ENC28J1.INT, ENC28J1.SO
  N4: Part1.D13/SCK, ENC28J1.SCK
  N5: Part1.D2, U1.DB4
  N6: Part1.D3_PWM, U1.DB5
  N7: Part1.D4, U1.DB6
  N8: Part1.D5_PWM, U1.DB7
  N9: Part1.D6_PWM, U1.RS
  N10: Part1.D7, U1.E
  5V: Part1.5V, U1.VDD, U1.A, ENC28J1.5v
  N11: U1.VO, R1.Pin_0

custom parts:
  ENC28J60: Ethernet Module ENC28J60
